// Logisim project arhitectura_sistem.circ as structural Verilog: 6 circuits, main circuit NodeMCU
module main (
  input  in_1,
  input  in_2,
  input  in_3,
  input  in_4,
  input  in_5,
  input  in_6,
  input  in_7,
  input  mod,
  input  in_9,
  output WIFI,
  output SERVO_intrare,
  output SERVO_iesire
);

  wire matrix_mux_1_out_4, matrix_mux_1_out_5, matrix_mux_1_out_6, matrix_mux_1_out_7, matrix_mux_1_out_8,
       matrix_mux_1_out_9, matrix_mux_1_out_10, matrix_mux_1_out_11, matrix_mux_1_out_12,
       matrix_mux_1_out_13, matrix_mux_1_out_14, matrix_mux_1_out_15, matrix_mux_1_out_16,
       matrix_mux_1_out_17, matrix_mux_1_out_18, matrix_mux_1_out_19, nodemcu_1_a0, nodemcu_1_d3,
       nodemcu_1_d4, nodemcu_1_d5_sck, nodemcu_1_d6_miso, nodemcu_1_d7_mosi, nodemcu_1_d8_cs;

  NodeMCU nodemcu_1 (
    .WIFI(WIFI), .A0(nodemcu_1_a0), .D0(mod), .D1(SERVO_intrare), .D2(SERVO_iesire), .D3(nodemcu_1_d3),
    .D4(nodemcu_1_d4), .D5_SCK(nodemcu_1_d5_sck), .D6_MISO(nodemcu_1_d6_miso), .D7_MOSI(nodemcu_1_d7_mosi),
    .D8_CS(nodemcu_1_d8_cs));  // open: RX, TX
  RFID RFID_intrare (.CS(nodemcu_1_d3), .MISO(nodemcu_1_d6_miso), .MOSI(nodemcu_1_d7_mosi), .SCK(nodemcu_1_d5_sck));
  RFID RFID_iesire (.CS(nodemcu_1_d4), .MISO(nodemcu_1_d6_miso), .MOSI(nodemcu_1_d7_mosi), .SCK(nodemcu_1_d5_sck));
  Matrix_MUX matrix_mux_1 (
    .DI(nodemcu_1_d7_mosi), .CLK(nodemcu_1_d5_sck), .CS_LOAD(nodemcu_1_d8_cs), .out_4(matrix_mux_1_out_4),
    .out_5(matrix_mux_1_out_5), .out_6(matrix_mux_1_out_6), .out_7(matrix_mux_1_out_7),
    .out_8(matrix_mux_1_out_8), .out_9(matrix_mux_1_out_9), .out_10(matrix_mux_1_out_10),
    .out_11(matrix_mux_1_out_11), .out_12(matrix_mux_1_out_12), .out_13(matrix_mux_1_out_13),
    .out_14(matrix_mux_1_out_14), .out_15(matrix_mux_1_out_15), .out_16(matrix_mux_1_out_16),
    .out_17(matrix_mux_1_out_17), .out_18(matrix_mux_1_out_18), .out_19(matrix_mux_1_out_19));
  LEDs leds_1 (
    .in_1(matrix_mux_1_out_12), .in_2(matrix_mux_1_out_13), .in_3(matrix_mux_1_out_14),
    .in_4(matrix_mux_1_out_15), .in_5(matrix_mux_1_out_16), .in_6(matrix_mux_1_out_17),
    .in_7(matrix_mux_1_out_18), .in_8(matrix_mux_1_out_19));
  MUX_gates mux_gates_1 (
    .A1(matrix_mux_1_out_4), .B1(in_1), .A2(matrix_mux_1_out_5), .B2(in_2), .A3(matrix_mux_1_out_6),
    .B3(in_3), .A4(matrix_mux_1_out_7), .B4(in_4), .A5(matrix_mux_1_out_8), .B5(in_5),
    .A6(matrix_mux_1_out_9), .B6(in_6), .A7(matrix_mux_1_out_10), .B7(in_7), .A8(matrix_mux_1_out_11),
    .B8(in_9), .IR(nodemcu_1_a0));
endmodule

module NodeMCU (
  output WIFI,
  output A0,
  output D0,
  output D1,
  output D2,
  output D3,
  output D4,
  output D5_SCK,
  output D6_MISO,
  output D7_MOSI,
  output D8_CS,
  output RX,
  output TX
);
endmodule

module RFID (
  output CS,
  output MISO,
  output MOSI,
  output SCK
);
endmodule

module Matrix_MUX (
  output DI,
  output CLK,
  output CS_LOAD,
  output out_4,
  output out_5,
  output out_6,
  output out_7,
  output out_8,
  output out_9,
  output out_10,
  output out_11,
  output out_12,
  output out_13,
  output out_14,
  output out_15,
  output out_16,
  output out_17,
  output out_18,
  output out_19
);
endmodule

module MUX_gates (
  input  A1,
  input  B1,
  input  A2,
  input  B2,
  input  A3,
  input  B3,
  input  A4,
  input  B4,
  input  A5,
  input  B5,
  input  A6,
  input  B6,
  input  A7,
  input  B7,
  input  A8,
  input  B8,
  output IR
);

  wire and_1_out, and_2_out, and_3_out, and_4_out, and_5_out, and_6_out, and_7_out, and_8_out;

  and and_1 (and_1_out, A1, B1);
  and and_2 (and_2_out, A2, B2);
  and and_3 (and_3_out, A3, B3);
  or or_1 (IR, and_1_out, and_2_out, and_3_out, and_4_out, and_5_out, and_6_out, and_7_out, and_8_out);
  and and_4 (and_4_out, A4, B4);
  and and_5 (and_5_out, A5, B5);
  and and_6 (and_6_out, A6, B6);
  and and_7 (and_7_out, A7, B7);
  and and_8 (and_8_out, A8, B8);
endmodule

module LEDs (
  input  in_1,
  input  in_2,
  input  in_3,
  input  in_4,
  input  in_5,
  input  in_6,
  input  in_7,
  input  in_8
);
endmodule
